# Fritzing sketch Jack (saved by Fritzing 0.9.3b)

parts:
  Part1 = Arduino Pro Mini v13
  DFRobot_DFPlayer_Mini1 = DFRobot DFPlayer Mini [part_number=DFR0299]
  PIR1 = PIR sensor
  SP1 = SPEAKER [package=pcb_mount_speaker]
  R1 = Resistor [tolerance=±5% resistance=220 package="2512 [SMD]"]
  J1 = Basic Servo
  JACK1 = 2.1mm DC Barrel Jack
  Part2 = 12 NeoPixel Ring [part_number=1643]
  S1 = Round Pushbutton
  R2 = Resistor [tolerance=±5% resistance=330 package="2512 [SMD]"]
  C1 = Electrolytic Capacitor [capacitance=1000μF package="1010 [SMD, electrolytic]"]

nets:
  VCC: Part1.VCC, DFRobot_DFPlayer_Mini1.VCC, PIR1.VDD, J1.vcc, JACK1.center, Part2.VDD, C1.+
  GND: Part1.GND, DFRobot_DFPlayer_Mini1.GND-1, DFRobot_DFPlayer_Mini1.SPK_2, DFRobot_DFPlayer_Mini1.IO_1, DFRobot_DFPlayer_Mini1.GND-2, DFRobot_DFPlayer_Mini1.IO_2, PIR1.GND, SP1.+, J1.gnd, JACK1.sleeve, Part2.GND, S1.leg1, C1.-
  N1: Part1.D12/MISO, DFRobot_DFPlayer_Mini1.TX, DFRobot_DFPlayer_Mini1.DAC_R
  N2: Part1.D11_PWM/MOSI, R1.Pin_0
  N3: Part1.D10_PWM/SS, DFRobot_DFPlayer_Mini1.USB_NEG, DFRobot_DFPlayer_Mini1.BUSY
  N4: Part1.D9_PWM, J1.pulse
  N5: Part1.D8, R2.Pin_0
  N6: Part1.D7, PIR1.SIG
  N7: Part1.D4, S1.leg0
  N8: DFRobot_DFPlayer_Mini1.RX, R1.Pin_1
  N9: DFRobot_DFPlayer_Mini1.DAC_L, DFRobot_DFPlayer_Mini1.SPK_1, SP1.-
  N10: Part2.IN, R2.Pin_1

custom parts:
  2.1mm DC Barrel Jack: 2.1mm DC Barrel Jack with Thru-Hole Connectors (breadboardable)
  12 NeoPixel Ring: 12 ultra bright smart LED NeoPixels are arranged in a circle with 1.5" (37mm) outer diameter. The rings are 'chainable' - connect the output pin of one to the input pin of another. Use only one microcontroller pin to control as many as you can chain together! Each LED is addressable as the driver chip is inside the LED. Each one has ~18mA constant current drive so the color will be very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
